# Fritzing sketch SerialLED_MiniPro (saved by Fritzing 0.9.3b)
breadboards: 1

parts:
  元件1 = Arduino Nano (Rev3.0) (ICSP)
  R1 = Resistor [tolerance=±5% resistance=220 package=THT]
  LED1 = LED - 5mm [color="Red (633nm)" package="5 mm [THT]"]
  RGB_SMD_LED1 = SMD RGB LED (WS2812) [package=5050]  # not connected
  J2 = Piezo Speaker  # not connected
  DFPlayerMini3 = DFPlayerMini

nets:
  GND: 元件1.GND, LED1.cathode, DFPlayerMini3.GND
  N1: 元件1.D2, DFPlayerMini3.DI
  N2: 元件1.D3, DFPlayerMini3.CS
  5V: 元件1.5V, DFPlayerMini3.VCC
  N3: 元件1.A1, R1.Pin_1, LED1.anode
  N4: 元件1.D13/SCK, R1.Pin_0

custom parts:
  DFPlayerMini: Breakout board for the microSD socket that is not much bigger than your fingernail. Compatible with the SPI interface found on any SD card, this tiny form factor was created for cell phone storage and is perfect for your next MP3 project! Board comes fully assembled and tested. The bare socket is available.
